// Logisim project 조별과제 (2) (4) (2) (4).circ as structural Verilog: 1 circuit, main circuit main
module main (
  input  in_1,
  output Power_Output,
  output out_3,
  output [3:0] Timer,
  output out_5,
  output out_6,
  output out_7,
  output activate_Motor_clockwise,
  output activate_Motor_counterclockwise,
  output [2:0] Amount_of_power_supplied_to_the_motor,
  output out_11
);

  wire a_out, and_1_out, and_2_out, and_3_out, and_4_out, and_5_out, and_6_out, and_7_out, and_8_out,
       and_9_out, and_10_out, and_11_out, and_12_out, and_13_out, and_14_out, and_15_out, and_16_out,
       and_17_out, and_18_out, and_19_out, and_20_out, and_21_out, and_22_out, and_23_out, and_28_out,
       and_29_out, and_30_out, and_31_out, and_33_out, and_34_out, and_35_out, and_36_out, and_37_out,
       and_38_out, and_39_out, and_40_out, and_41_out, and_42_out, b_out, button_1_out, button_2_out, c_out,
       clock_1_out, d_ff_1_q, d_ff_2_q, d_ff_3_q, d_ff_4_q, d_out, e_out, f_out, g_out, j_k_ff_1_qn,
       j_k_ff_2_qn, nand_1_out, nand_2_out, nand_4_out, not_1_out, not_2_out, not_3_out, not_4_out,
       not_5_out, not_6_out, not_7_out, not_8_out, or_1_out, or_2_out, or_3_out, or_4_out, or_5_out,
       or_6_out, or_7_out, or_8_out, s_r_ff_1_q, xor_1_out;
  wire [1:0] joystick_1_x, joystick_1_y;

  not not_1 (not_1_out, in_1);
  and and_1 (and_1_out, button_1_out, or_1_out);
  or or_1 (or_1_out, Amount_of_power_supplied_to_the_motor[2], Amount_of_power_supplied_to_the_motor[1], Amount_of_power_supplied_to_the_motor[0]);
  not not_2 (not_2_out, s_r_ff_1_q);
  Joystick #(.bits(2)) joystick_1 (.x(joystick_1_x), .y(joystick_1_y));
  _7_Segment_Display u_7_segment_display_1 (
    .g(and_5_out), .f(and_17_out), .a(and_42_out), .b(and_39_out), .e(and_22_out), .d(and_31_out),
    .c(and_37_out), .dp(1'b0));
  and and_2 (and_2_out, Amount_of_power_supplied_to_the_motor[2], not_6_out);
  Button button_1 (.out(button_1_out));
  or or_2 (or_2_out, and_1_out, and_6_out);
  J_K_Flip_Flop #(.trigger("falling")) j_k_ff_1 (
    .J(1'b1), .clk(or_2_out), .K(1'b1), .Q(Amount_of_power_supplied_to_the_motor[0]), .Qn(j_k_ff_1_qn),
    .reset(not_1_out));  // open: preset, en
  and and_3 (and_3_out, Amount_of_power_supplied_to_the_motor[2], not_7_out);
  and and_4 (and_4_out, not_5_out, Amount_of_power_supplied_to_the_motor[1]);
  or g (g_out, and_2_out, and_3_out, and_4_out, and_9_out);
  and and_5 (and_5_out, g_out, in_1);
  Button button_2 (.out(button_2_out));
  and and_6 (and_6_out, button_2_out, nand_1_out);
  nand nand_1 (nand_1_out, Amount_of_power_supplied_to_the_motor[0], ~Amount_of_power_supplied_to_the_motor[1], Amount_of_power_supplied_to_the_motor[2]);  // NAND_Gate
  and and_7 (and_7_out, s_r_ff_1_q, Amount_of_power_supplied_to_the_motor[0]);
  and and_8 (and_8_out, j_k_ff_1_qn, not_2_out);
  and and_9 (and_9_out, Amount_of_power_supplied_to_the_motor[1], not_7_out);
  S_R_Flip_Flop #(.trigger("high")) s_r_ff_1 (
    .S(button_2_out), .clk(1'b1), .R(button_1_out), .Q(s_r_ff_1_q), .reset(not_3_out));  // open: Qn, preset, en
  or or_3 (or_3_out, or_2_out, or_5_out);
  and and_10 (and_10_out, Amount_of_power_supplied_to_the_motor[2], not_6_out);
  or or_4 (or_4_out, and_7_out, and_8_out);
  and and_11 (and_11_out, joystick_1_y[0], ~joystick_1_y[1]);  // AND_Gate
  and and_12 (and_12_out, joystick_1_y[0], joystick_1_y[1]);
  and and_13 (and_13_out, joystick_1_x[0], ~joystick_1_x[1]);  // AND_Gate
  and and_14 (and_14_out, joystick_1_x[0], joystick_1_x[1]);
  and and_15 (and_15_out, Amount_of_power_supplied_to_the_motor[2], not_7_out);
  and and_16 (and_16_out, not_6_out, not_7_out);
  or f (f_out, and_10_out, and_15_out, and_16_out);
  and and_17 (and_17_out, f_out, in_1);
  xor xor_1 (xor_1_out, in_1, or_3_out);
  J_K_Flip_Flop #(.trigger("falling")) j_k_ff_2 (
    .J(or_4_out), .clk(or_2_out), .K(or_4_out), .Q(Amount_of_power_supplied_to_the_motor[1]),
    .Qn(j_k_ff_2_qn), .reset(not_1_out));  // open: preset, en
  or or_5 (or_5_out, and_11_out, and_12_out, and_13_out, and_14_out);
  and and_18 (and_18_out, not_5_out, not_7_out);
  or e (e_out, and_18_out, and_21_out);
  LED led_1 (.in(or_6_out));
  or or_6 (or_6_out, in_1, Power_Output);
  nand nand_2 (nand_2_out, xor_1_out, out_3);
  nand nand_3 (out_3, nand_2_out, nand_4_out);
  and and_19 (and_19_out, and_7_out, Amount_of_power_supplied_to_the_motor[1]);
  and and_20 (and_20_out, j_k_ff_2_qn, and_8_out);
  D_Flip_Flop d_ff_1 (.clk(and_11_out), .D(and_11_out), .Q(d_ff_1_q), .reset(not_3_out));  // open: Qn, preset, en
  D_Flip_Flop d_ff_2 (.clk(and_12_out), .D(and_12_out), .Q(d_ff_2_q), .reset(not_3_out));  // open: Qn, preset, en
  D_Flip_Flop d_ff_3 (.clk(and_13_out), .D(and_13_out), .Q(d_ff_3_q), .reset(not_3_out));  // open: Qn, preset, en
  D_Flip_Flop d_ff_4 (.clk(and_14_out), .D(and_14_out), .Q(d_ff_4_q), .reset(not_3_out));  // open: Qn, preset, en
  and and_21 (and_21_out, Amount_of_power_supplied_to_the_motor[1], not_7_out);
  and and_22 (and_22_out, e_out, in_1);
  LED led_2 (.in(and_23_out));
  and and_23 (and_23_out, in_1, ~Power_Output);  // AND_Gate
  or or_7 (or_7_out, and_19_out, and_20_out);
  and and_24 (activate_Motor_clockwise, and_11_out, d_ff_1_q);
  and and_25 (activate_Motor_counterclockwise, d_ff_2_q, and_12_out);
  and and_26 (out_7, and_13_out, d_ff_3_q);
  and and_27 (out_11, d_ff_4_q, and_14_out);
  and and_28 (and_28_out, not_5_out, Amount_of_power_supplied_to_the_motor[1]);
  and and_29 (and_29_out, Amount_of_power_supplied_to_the_motor[1], not_7_out);
  J_K_Flip_Flop #(.trigger("falling")) j_k_ff_3 (
    .J(or_7_out), .clk(or_2_out), .K(or_7_out), .Q(Amount_of_power_supplied_to_the_motor[2]),
    .reset(not_1_out));  // open: Qn, preset, en
  and and_30 (and_30_out, not_5_out, not_7_out);
  or d (d_out, and_28_out, and_29_out, and_30_out, and_33_out);
  and and_31 (and_31_out, d_out, in_1);
  and and_32 (Power_Output, nand_2_out, in_1);
  and and_33 (and_33_out, Amount_of_power_supplied_to_the_motor[2], not_6_out, Amount_of_power_supplied_to_the_motor[0]);
  not not_3 (not_3_out, Power_Output);
  and and_34 (and_34_out, and_35_out, Timer[2]);
  and and_35 (and_35_out, Timer[0], Timer[1]);
  not not_4 (not_4_out, or_5_out);
  not not_5 (not_5_out, Amount_of_power_supplied_to_the_motor[2]);
  not not_6 (not_6_out, Amount_of_power_supplied_to_the_motor[1]);
  not not_7 (not_7_out, Amount_of_power_supplied_to_the_motor[0]);
  and and_36 (and_36_out, Amount_of_power_supplied_to_the_motor[1], Amount_of_power_supplied_to_the_motor[0]);
  or c (c_out, Amount_of_power_supplied_to_the_motor[2], not_6_out, Amount_of_power_supplied_to_the_motor[0]);
  and and_37 (and_37_out, c_out, in_1);
  or or_8 (or_8_out, not_3_out, not_8_out);
  Clock clock_1 (.out(clock_1_out));
  and and_38 (and_38_out, not_6_out, not_7_out);
  or b (b_out, and_36_out, not_5_out, and_38_out);
  and and_39 (and_39_out, b_out, in_1);
  nand nand_4 (nand_4_out, Timer[3], Timer[2], Timer[1], Timer[0]);
  J_K_Flip_Flop j_k_ff_4 (
    .J(and_34_out), .clk(clock_1_out), .K(and_34_out), .Q(Timer[3]), .reset(or_8_out));  // open: Qn, preset, en
  J_K_Flip_Flop j_k_ff_5 (
    .J(and_35_out), .clk(clock_1_out), .K(and_35_out), .Q(Timer[2]), .reset(or_8_out));  // open: Qn, preset, en
  J_K_Flip_Flop j_k_ff_6 (
    .J(Timer[0]), .clk(clock_1_out), .K(Timer[0]), .Q(Timer[1]), .reset(or_8_out));  // open: Qn, preset, en
  J_K_Flip_Flop j_k_ff_7 (
    .J(not_4_out), .clk(clock_1_out), .K(not_4_out), .Q(Timer[0]), .reset(or_8_out));  // open: Qn, preset, en
  and and_40 (and_40_out, Amount_of_power_supplied_to_the_motor[2], Amount_of_power_supplied_to_the_motor[0]);
  not not_8 (not_8_out, not_4_out);
  and and_41 (and_41_out, not_5_out, not_7_out);
  or a (a_out, and_40_out, Amount_of_power_supplied_to_the_motor[1], and_41_out);
  and and_42 (and_42_out, a_out, in_1);

  assign out_5 = activate_Motor_clockwise;
  assign out_6 = activate_Motor_counterclockwise;

  // Notes on the sheet:
  //   Power Input
  //   Joystick(Direction)
  //   Speed Indicator(Output)
  //   h
  //   Speed decrease
  //   Speed Limit (=0~5)
  //   Speed increase
  //   On(green)/Off(red)
  //   Mode
  //   Idle
  //   Left(direction of frontwheel)
  //   Right(direction of fronwheel)
  //   Frontward(direction of fronwheel)
  //   Backward(direction of frontwheel)
endmodule
